// Logisim project TME1.circ as structural Verilog: 6 circuits, main circuit MUX2
module MUX2 (
  input  in_1,
  input  in_2,
  input  in_3,
  output out_4
);

  wire and_1_out, ET_NON_out_3;

  and and_1 (and_1_out, in_1, in_3);
  ETNON ET_NON (.in_1(in_2), .in_2(in_1), .out_3(ET_NON_out_3));
  or OU (out_4, ET_NON_out_3, and_1_out);
endmodule

module mon_xor (
  input  in_1,
  input  in_2,
  output out_3
);

  wire etnon_1_out_3, etnon_2_out_3;

  ETNON etnon_1 (.in_1(in_1), .in_2(in_2), .out_3(etnon_1_out_3));
  ETNON etnon_2 (.in_1(in_2), .in_2(in_1), .out_3(etnon_2_out_3));
  or or_1 (out_3, etnon_1_out_3, etnon_2_out_3);
endmodule

module ETNON (
  input  in_1,
  input  in_2,
  output out_3
);

  wire not_1_out;

  not not_1 (not_1_out, in_2);
  and and_1 (out_3, in_1, not_1_out);
endmodule

module mux2sur4bits (
  input  in_1,
  input  in_2,
  input  in_3,
  input  in_4,
  input  in_5,
  input  in_6,
  input  in_7,
  input  in_8,
  input  in_9,
  output out_10,
  output out_11,
  output out_12,
  output out_13
);

  MUX2 mux2 (.in_2(in_2), .in_3(in_6), .in_1(in_1), .out_4(out_10));
  MUX2 mux2_2 (.in_2(in_3), .in_3(in_7), .in_1(in_1), .out_4(out_11));
  MUX2 mux2_3 (.in_2(in_4), .in_3(in_8), .in_1(in_1), .out_4(out_12));
  MUX2 mux2_4 (.in_2(in_5), .in_3(in_9), .in_1(in_1), .out_4(out_13));
endmodule

module mux4vers1 (
  input  in_1,
  input  in_2,
  input  in_3,
  input  in_4,
  input  in_5,
  input  in_6,
  output out_7
);

  wire mux2_1_out_4, mux2_2_out_4;

  MUX2 mux2_1 (.in_2(in_3), .in_3(in_4), .in_1(in_2), .out_4(mux2_1_out_4));
  MUX2 mux2_2 (.in_2(in_5), .in_3(in_6), .in_1(in_2), .out_4(mux2_2_out_4));
  MUX2 mux2_3 (.in_2(mux2_1_out_4), .in_3(mux2_2_out_4), .in_1(in_1), .out_4(out_7));
endmodule

module machine_caffe (
  input  CQFFE,
  input  SUCRE,
  input  BOUILLON,
  output ERROR_LAMP
);

  wire and_1_out, and_2_out, not_1_out, not_2_out;

  not not_1 (not_1_out, CQFFE);
  not not_2 (not_2_out, SUCRE);
  and and_1 (and_1_out, SUCRE, not_1_out);
  and and_2 (and_2_out, CQFFE, not_2_out, BOUILLON);
  or or_1 (ERROR_LAMP, and_1_out, and_2_out);
endmodule
