// Logisim project TME3.circ as structural Verilog
module ALU (
  input  SELECTEUR,
  input  [3:0] A,
  input  [3:0] B,
  output [3:0] S,
  output CF,
  output OV,
  output ZF,
  output SF
);

  wire add_1_bit_complet_1_out_5, add_1_bit_complet_2_out_5, add_1_bit_complet_3_out_5, comp_4bits_1_a_b,
       or_1_out, xor_1_out, xor_2_out, xor_3_out, xor_4_out;

  xor xor_1 (xor_1_out, SELECTEUR, B[0]);
  xor xor_2 (xor_2_out, SELECTEUR, B[1]);
  xor xor_3 (xor_3_out, SELECTEUR, B[2]);
  xor xor_4 (xor_4_out, SELECTEUR, B[3]);
  COMP_4BITS comp_4bits_1 (.A(A), .B(B), .A_B(comp_4bits_1_a_b));  // open: A___B, A___B_2
  ADD_1_bit_complet add_1_bit_complet_1 (
    .in_2(A[0]), .in_3(xor_1_out), .in_1(SELECTEUR), .out_5(add_1_bit_complet_1_out_5), .out_4(S[0]));
  ADD_1_bit_complet add_1_bit_complet_2 (
    .in_2(A[1]), .in_3(xor_2_out), .in_1(add_1_bit_complet_1_out_5), .out_5(add_1_bit_complet_2_out_5),
    .out_4(S[1]));
  ADD_1_bit_complet add_1_bit_complet_3 (
    .in_2(A[2]), .in_3(xor_3_out), .in_1(add_1_bit_complet_2_out_5), .out_5(add_1_bit_complet_3_out_5),
    .out_4(S[2]));
  ADD_1_bit_complet add_1_bit_complet_4 (
    .in_2(A[3]), .in_3(xor_4_out), .in_1(add_1_bit_complet_3_out_5), .out_5(CF), .out_4(S[3]));
  or or_1 (or_1_out, S[0], S[1], S[2], S[3]);
  not not_1 (ZF, or_1_out);
  mon_xor mon_xor_1 (.in_1(CF), .in_2(add_1_bit_complet_3_out_5), .out_3(OV));
  and and_1 (SF, SELECTEUR, comp_4bits_1_a_b);
endmodule

// S
module DEC_droite (
  input  in_1,
  input  in_2,
  input  [3:0] in_3,
  output s0,
  output s1,
  output s2,
  output s3
);

  wire and_1_out, and_2_out, nor_1_out, not_1_out;

  mux4vers1 mux4vers1_1 (
    .in_3(in_3[0]), .in_4(in_3[1]), .in_5(in_3[2]), .in_6(in_3[3]), .in_1(in_1), .in_2(in_2), .out_7(s0));
  mux4vers1 mux4vers1_2 (
    .in_3(in_3[1]), .in_4(in_3[2]), .in_5(in_3[3]), .in_6(in_3[3]), .in_1(in_1), .in_2(in_2), .out_7(s1));
  nor nor_1 (nor_1_out, in_2, in_1);
  and and_1 (and_1_out, nor_1_out, in_3[2]);
  not not_1 (not_1_out, nor_1_out);
  and and_2 (and_2_out, not_1_out, in_3[3]);
  or or_1 (s2, and_2_out, and_1_out);

  assign s3 = in_3[3];
endmodule

module DEC_gauche (
  input  i1,
  input  i0,
  input  [3:0] E,
  output [3:0] S
);

  wire and_2_out, and_3_out, not_1_out, not_2_out;

  mux4vers1 mux4vers1_1 (.in_3(E[2]), .in_4(E[1]), .in_5(E[0]), .in_6(1'b0), .in_1(i1), .in_2(i0), .out_7(S[2]));
  mux4vers1 mux4vers1_2 (.in_3(E[3]), .in_4(E[2]), .in_5(E[1]), .in_6(E[0]), .in_1(i1), .in_2(i0), .out_7(S[3]));
  not not_1 (not_1_out, i0);
  not not_2 (not_2_out, i1);
  and and_1 (S[0], not_1_out, E[0], not_2_out);
  and and_2 (and_2_out, not_2_out, not_1_out, E[1]);
  and and_3 (and_3_out, not_2_out, i0, E[0]);
  or or_1 (S[1], and_2_out, and_3_out);
endmodule

module Comparateur_1bit (
  input  EIN,
  input  a,
  input  b,
  output A_B,
  output A_B_2,
  output A_B_3,
  output E_out
);

  wire mon_xor_1_out_3, not_1_out, not_2_out;

  not not_1 (not_1_out, b);
  mon_xor mon_xor_1 (.in_1(a), .in_2(b), .out_3(mon_xor_1_out_3));
  not not_2 (not_2_out, a);
  not not_3 (A_B_3, mon_xor_1_out_3);
  and and_1 (A_B, a, not_1_out);
  and and_2 (A_B_2, not_2_out, b);
  and and_3 (E_out, A_B_3, EIN);
endmodule

module COMP_4BITS (
  input  [3:0] A,
  input  [3:0] B,
  output A___B,
  output A_B,
  output A___B_2
);

  wire and_2_out, and_3_out, and_4_out, and_5_out, and_6_out, and_7_out, comparateur_1bit_1_a_b,
       comparateur_1bit_1_a_b_2, comparateur_1bit_1_a_b_3, comparateur_1bit_1_e_out, comparateur_1bit_2_a_b,
       comparateur_1bit_2_a_b_2, comparateur_1bit_2_a_b_3, comparateur_1bit_2_e_out, comparateur_1bit_3_a_b,
       comparateur_1bit_3_a_b_2, comparateur_1bit_3_a_b_3, comparateur_1bit_3_e_out, comparateur_1bit_4_a_b,
       comparateur_1bit_4_a_b_2, comparateur_1bit_4_a_b_3;

  Comparateur_1bit comparateur_1bit_1 (
    .a(A[3]), .b(B[3]), .EIN(1'b1), .E_out(comparateur_1bit_1_e_out), .A_B(comparateur_1bit_1_a_b),
    .A_B_2(comparateur_1bit_1_a_b_2), .A_B_3(comparateur_1bit_1_a_b_3));
  Comparateur_1bit comparateur_1bit_2 (
    .a(A[2]), .b(B[2]), .EIN(comparateur_1bit_1_e_out), .E_out(comparateur_1bit_2_e_out),
    .A_B(comparateur_1bit_2_a_b), .A_B_2(comparateur_1bit_2_a_b_2), .A_B_3(comparateur_1bit_2_a_b_3));
  Comparateur_1bit comparateur_1bit_3 (
    .a(A[1]), .b(B[1]), .EIN(comparateur_1bit_2_e_out), .E_out(comparateur_1bit_3_e_out),
    .A_B(comparateur_1bit_3_a_b), .A_B_2(comparateur_1bit_3_a_b_2), .A_B_3(comparateur_1bit_3_a_b_3));
  Comparateur_1bit comparateur_1bit_4 (
    .a(A[0]), .b(B[0]), .EIN(comparateur_1bit_3_e_out), .A_B(comparateur_1bit_4_a_b),
    .A_B_2(comparateur_1bit_4_a_b_2), .A_B_3(comparateur_1bit_4_a_b_3));  // open: E_out
  and and_1 (A___B_2, comparateur_1bit_1_a_b_3, comparateur_1bit_2_a_b_3, comparateur_1bit_3_a_b_3, comparateur_1bit_4_a_b_3);
  and and_2 (and_2_out, comparateur_1bit_2_a_b, comparateur_1bit_1_e_out);
  and and_3 (and_3_out, comparateur_1bit_2_e_out, comparateur_1bit_3_a_b);
  and and_4 (and_4_out, comparateur_1bit_3_e_out, comparateur_1bit_4_a_b);
  and and_5 (and_5_out, comparateur_1bit_1_e_out, comparateur_1bit_2_a_b_2);
  and and_6 (and_6_out, comparateur_1bit_2_e_out, comparateur_1bit_3_a_b_2);
  and and_7 (and_7_out, comparateur_1bit_3_e_out, comparateur_1bit_4_a_b_2);
  or or_1 (A_B, comparateur_1bit_1_a_b_2, and_5_out, and_6_out, and_7_out);
  or or_2 (A___B, comparateur_1bit_1_a_b, and_2_out, and_3_out, and_4_out);
endmodule
