// Logisim project TME4.circ as structural Verilog: 4 circuits, main circuit Registre 4 bits
module Registre_4_bits (
  input  [3:0] Din,
  input  WE,
  input  clk,
  output [3:0] Dout
);

  Register #(.width(4)) register_1 (.D(Din), .en(WE), .Q(Dout), .clk(clk), .clr(1'b0));
endmodule

module \Chemin_de_Données  (
  input  [3:0] DIN_A,
  input  EXT_A,
  input  WE_A,
  input  [3:0] DIN_B,
  input  EXT_B,
  input  WE_B,
  input  [3:0] DIN_C,
  input  EXT_C,
  input  WE_c,
  input  [1:0] OP_X,
  input  [1:0] OP_Y,
  input  ADD_SUB,
  input  [3:0] DIN_D,
  input  EXT_D,
  input  WE_D,
  output CF,
  output OV,
  output ZF,
  output SF
);

  wire clock_1_out, mux2sur4bits_1_p1;
  wire [3:0] mux2sur4bits_1_p4, mux2sur4bits_2_p4, mux2sur4bits_3_p4, mux2sur4bits_4_p4, mux32vers4_1_out_6,
       mux32vers4_2_out_6, RA_dout, RB_dout, RC_dout, RD_dout;

  // mux2sur4bits mux2sur4bits_1: pin names not known; wires that end beside it: mux2sur4bits_1_p1, DIN_A, EXT_A, mux2sur4bits_1_p4[0], mux2sur4bits_1_p4[1], mux2sur4bits_1_p4[2], mux2sur4bits_1_p4[3]
  // mux2sur4bits mux2sur4bits_2: pin names not known; wires that end beside it: mux2sur4bits_1_p1, DIN_B, EXT_B, mux2sur4bits_2_p4[0], mux2sur4bits_2_p4[1], mux2sur4bits_2_p4[2], mux2sur4bits_2_p4[3]
  // mux2sur4bits mux2sur4bits_3: pin names not known; wires that end beside it: mux2sur4bits_1_p1, DIN_C, EXT_C, mux2sur4bits_3_p4[0], mux2sur4bits_3_p4[1], mux2sur4bits_3_p4[2], mux2sur4bits_3_p4[3]
  // mux2sur4bits mux2sur4bits_4: pin names not known; wires that end beside it: mux2sur4bits_1_p1, DIN_D, EXT_D, mux2sur4bits_4_p4[0], mux2sur4bits_4_p4[1], mux2sur4bits_4_p4[2], mux2sur4bits_4_p4[3]
  Clock clock_1 (.out(clock_1_out));
  Registre_4_bits RA (.Din(mux2sur4bits_1_p4), .WE(WE_A), .clk(clock_1_out), .Dout(RA_dout));
  Registre_4_bits RB (.Din(mux2sur4bits_2_p4), .WE(WE_B), .clk(clock_1_out), .Dout(RB_dout));
  Registre_4_bits RC (.Din(mux2sur4bits_3_p4), .WE(WE_c), .clk(clock_1_out), .Dout(RC_dout));
  Registre_4_bits RD (.Din(mux2sur4bits_4_p4), .WE(WE_D), .clk(clock_1_out), .Dout(RD_dout));
  mux32vers4 mux32vers4_1 (.A(RA_dout), .B(RB_dout), .C(RC_dout), .D(RD_dout), .in_5(OP_X), .out_6(mux32vers4_1_out_6));
  mux32vers4 mux32vers4_2 (.A(RA_dout), .B(RB_dout), .C(RC_dout), .D(RD_dout), .in_5(OP_Y), .out_6(mux32vers4_2_out_6));
  // ALU alu_1: pin names not known; wires that end beside it: mux32vers4_1_out_6, mux32vers4_2_out_6, ADD_SUB, mux2sur4bits_1_p1, CF, OV, ZF, SF
endmodule

// MUX 32 vers 4
module mux32vers4 (
  input  [3:0] A,
  input  [3:0] B,
  input  [3:0] C,
  input  [3:0] D,
  input  [1:0] in_5,
  output [3:0] out_6
);

  wire mux2sur4bits_1_p3, mux2sur4bits_1_p4;
  wire [3:0] mux2sur4bits_1_p7, mux2sur4bits_2_p6;

  // mux2sur4bits mux2sur4bits_1: pin names not known; wires that end beside it: A, B, mux2sur4bits_1_p3, mux2sur4bits_1_p4, in_5[0], in_5[0], mux2sur4bits_1_p7[0], mux2sur4bits_1_p7[1], mux2sur4bits_1_p7[2], mux2sur4bits_1_p7[3]
  // mux2sur4bits mux2sur4bits_2: pin names not known; wires that end beside it: mux2sur4bits_1_p3, mux2sur4bits_1_p4, C, D, in_5[0], mux2sur4bits_2_p6[0], mux2sur4bits_2_p6[1], mux2sur4bits_2_p6[2], mux2sur4bits_2_p6[3]
  // mux2sur4bits mux2sur4bits_3: pin names not known; wires that end beside it: mux2sur4bits_1_p7, mux2sur4bits_2_p6, in_5[1], out_6[0], out_6[1], out_6[2], out_6[3]
endmodule

module RAM (
  input  [3:0] ADRESSE,
  input  [7:0] DIN,
  input  STORE,
  input  SEL,
  input  LOAD,
  input  CLR,
  output [7:0] DOUT
);

  wire clock_1_out;

  Clock clock_1 (.out(clock_1_out));
  RAM_part #(.addrWidth(4), .bus("separate")) ram_1 (
    .addr(ADRESSE), .din(DIN), .data(DOUT), .str(STORE), .sel(SEL), .clk(clock_1_out), .ld(LOAD), .clr(CLR));
endmodule
